# Fritzing sketch prototype (saved by Fritzing 0.9.1b)
breadboards: 1

parts:
  U2 = Spark Core (v1.0)
  LED1 = LED - 5mm [color="Infrared (850nm)" part_number="OSI5LA5113A " package="5 mm [THT]"]
  U3 = OSRB38C9AA - Infrared Receiver Module [part_number=OSRB38C9AA]

nets:
  N1: U2.A2, U2.3V3
  N2: U2.A3, U2.A6
  N3: U2.A5, U2.VIN
  N4: U2.A7, LED1.anode
  GND: U2.GND, LED1.cathode, U3.GND
  N5: U2.D7, U3.Output
  N6: U2.3V3*, U3.Vcc

custom parts:
  Spark Core (v1.0): The Spark Core is a tiny Wi-Fi development board that makes it easy to create internet-connected hardware. The Core is all you need to get started; power it over USB and in minutes you'll be controlling LEDs, switches and motors and collecting data from sensors over the internet! It has 8 digital I/O pins, 8 analog I/O pins, 8 PWM pins; UART (Serial), SPI, I2C, and JTAG peripherals available.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
